// Digital circuit tom-1.dig as structural Verilog
module tom_1 (
  input  clk,
  input  in_4,
  input  in_5,
  output pulse,
  output clk_2
);

  wire and_1_out, and_2_out, and_3_out, and_4_out, decoder_1_out_0, decoder_1_out_1, decoder_1_out_2,
       decoder_1_out_3, driver_1_out, nclk, not_2_out, not_3_out, not_4_out, not_5_out, npulse, nreset,
       nTOS_eq__eq_0_nis0, or_1_out, xor_1_out;
  wire [1:0] ROM_d;
  wire [7:0] D_REGISTER_q, PROGRAM_COUNTER_pc, PROGRAM_COUNTER_pc_2, tom_1_573_1_out, tom_1_573_2_out,
       tom_374_1_p1, tom_374_1_p2, tom_374_1_p4, tom_374_2_p1, tom_374_2_p4;
  wire [15:0] tom_1_373_2_p4, tom_374_3_p4;

  not not_1 (npulse, clk);
  Reset reset_1 (.out(nreset));
  LED led_1 (.in(npulse));
  // Probe on npulse
  LED led_2 (.in(clk));
  D_FF d_ff_1 (.D(clk_2), .C(npulse), .Q(nclk), .nQ(clk_2));
  LED led_3 (.in(nclk));
  LED led_4 (.in(clk_2));
  Break break_1 (.brk(driver_1_out));
  assign driver_1_out = in_5 ? npulse : 1'bz;  // Driver driver_1
  tom_1_is0 nTOS_eq__eq_0 (.\input ({tom_374_2_p4, tom_374_1_p4}), .nis0(nTOS_eq__eq_0_nis0));
  Decoder #(.Selector_Bits(2)) decoder_1 (
    .sel(ROM_d), .out_0(decoder_1_out_0), .out_1(decoder_1_out_1), .out_2(decoder_1_out_2),
    .out_3(decoder_1_out_3));
  and and_1 (and_1_out, tom_374_1_p2[4], clk);
  not not_2 (not_2_out, nTOS_eq__eq_0_nis0);
  // Probe tos_bus on {tom_374_2_p1, tom_374_1_p1}
  Break BREAK_2 (.brk(tom_374_1_p2[7]));
  not not_3 (not_3_out, tom_374_1_p2[1]);
  and and_2 (and_2_out, not_2_out, clk, tom_374_1_p2[7]);
  and and_3 (and_3_out, ~tom_374_1_p2[1], and_1_out);  // And
  and and_4 (and_4_out, ~not_3_out, and_1_out);  // And
  xor xor_1 (xor_1_out, nreset, and_2_out);
  // tom_374 tom_374_1: pin names not known; wires that end beside it: tom_374_1_p1, tom_374_1_p2[0], nclk, tom_374_1_p4
  // tom_374 tom_374_2: pin names not known; wires that end beside it: tom_374_2_p1, tom_374_1_p2[0], nclk, tom_374_2_p4
  // Probe CCK on and_1_out
  tom_1_d_r D_REGISTER (
    .nENP(1'b0), .nCCLR(nreset), .RCK(1'b0), .R_nC(1'b0), .nG(tom_374_1_p2[1]), .nLOAD(1'b1), .nENT(1'b0),
    .U_nD(tom_374_1_p2[2]), .D({8{1'b0}}), .CCK(and_3_out), .Q(D_REGISTER_q));
  tom_1_d_r R_REGISTER (
    .nENP(1'b0), .nCCLR(nreset), .RCK(1'b0), .R_nC(1'b0), .nG(not_3_out), .nLOAD(1'b1), .nENT(1'b0),
    .U_nD(tom_374_1_p2[2]), .D({8{1'b0}}), .CCK(and_4_out), .Q(D_REGISTER_q));
  // Probe dr on D_REGISTER_q
  tom_1_pc PROGRAM_COUNTER (
    .clk(npulse), .\input (tom_374_3_p4), .nLOAD(xor_1_out), .pc({PROGRAM_COUNTER_pc_2, PROGRAM_COUNTER_pc}));
  // Probe TOS on {tom_374_2_p4, tom_374_1_p4}
  SixteenSeg sixteenseg_1 (.led({tom_374_2_p4, tom_374_1_p4}), .dp(1'b0));
  tom_1_573 tom_1_573_1 (.C(npulse), .in(PROGRAM_COUNTER_pc), .out(tom_1_573_1_out));
  tom_1_573 tom_1_573_2 (.C(npulse), .in(PROGRAM_COUNTER_pc_2), .out(tom_1_573_2_out));
  not not_4 (not_4_out, tom_374_1_p2[3]);
  // Probe PC on {tom_1_573_2_out, tom_1_573_1_out}
  EEPROM #(.AddrBits(16), .isProgramMemory("true"), .Bits(16)) ROM (
    .A({tom_1_573_2_out, tom_1_573_1_out}), .CS(1'b1), .WE(1'b0), .OE(nreset),
    .D({tom_374_1_p2[7], ROM_d, tom_374_1_p2[4:0], tom_374_3_p4[7:0]}));
  or or_1 (or_1_out, decoder_1_out_1, not_4_out);
  // Probe ~d/r on tom_374_1_p2[1]
  // Probe ROM on tom_374_3_p4
  // tom_1_373 tom_1_373_1: pin names not known; wires that end beside it: tom_374_1_p4, or_1_out, 1'b1, tom_1_373_2_p4[7:0]
  // tom_1_373 tom_1_373_2: pin names not known; wires that end beside it: tom_374_2_p4, or_1_out, 1'b1, tom_1_373_2_p4[15:8]
  // Probe stack addr on {tom_374_1_p2[1], D_REGISTER_q}
  RAMSinglePortSel #(.AddrBits(9), .Bits(16)) STACK (
    .A({tom_374_1_p2[1], D_REGISTER_q}), .CS(1'b1), .WE(tom_374_1_p2[3]), .OE(not_4_out), .D(tom_1_373_2_p4));
  RAMSinglePortSel #(.AddrBits(16), .Bits(16)) RAM (
    .A({tom_374_2_p4, tom_374_1_p4}), .CS(decoder_1_out_1), .WE(not_4_out), .OE(tom_374_1_p2[3]),
    .D(tom_1_373_2_p4));
  // tom_374 tom_374_3: pin names not known; wires that end beside it: tom_374_3_p4[7:0], 1'b0, clk_2, tom_374_3_p4[15:8]
  // Probe CTRL on {tom_374_1_p2[7], ROM_d, tom_374_1_p2[4:0]}
  // Probe stack_bus on tom_1_373_2_p4
  tom_1_nand NAND (
    .A({tom_374_2_p4, tom_374_1_p4}), .B(tom_1_373_2_p4), .Vin(decoder_1_out_3),
    .out({tom_374_2_p1, tom_374_1_p1}));
  // tom_1_add tom_1_add_1: pin names not known; wires that end beside it: {tom_374_2_p4, tom_374_1_p4}, tom_1_373_2_p4, decoder_1_out_2, {tom_374_2_p1, tom_374_1_p1}
  not not_5 (not_5_out, decoder_1_out_0);
  // tom_1_373 tom_1_373_3: pin names not known; wires that end beside it: tom_374_3_p4[7:0], not_5_out, 1'b1, tom_374_1_p1
  // tom_1_373 tom_1_373_4: pin names not known; wires that end beside it: tom_374_3_p4[15:8], not_5_out, 1'b1, tom_374_2_p1

  assign pulse = clk;

  // Other names for the same wires on the sheet: clk_t = clk_2

  // Notes on the sheet:
  //   clk: Hz: 3
  //   in_5: default 1
  //   Clock
  //   CTRLs needed until PC latching works
  //   contents of ROM (hex, n*v repeats v):
  //   0,100,1c55,c66,1c11,c22,1cff,cff,1000,6000,1c00,c01,1000,4000,1000,4000,1000,4100,
  //   1c00,c00,1000,8000
endmodule
